// Digital circuit four_bit_adder.dig as structural Verilog
module four_bit_adder (
  input  cin,
  input  [3:0] a,
  input  [3:0] b,
  output cout,
  output [3:0] y,
  output overfl
);

  wire full_adder_2_cout, full_adder_3_cout, full_adder_4_cout;

  full_adder full_adder_1 (.a(a[3]), .b(b[3]), .cin(full_adder_2_cout), .cout(cout), .sum(y[3]));
  full_adder full_adder_2 (.a(a[2]), .b(b[2]), .cin(full_adder_3_cout), .cout(full_adder_2_cout), .sum(y[2]));
  full_adder full_adder_3 (.a(a[1]), .b(b[1]), .cin(full_adder_4_cout), .cout(full_adder_3_cout), .sum(y[1]));
  full_adder full_adder_4 (.a(a[0]), .b(b[0]), .cin(cin), .cout(full_adder_4_cout), .sum(y[0]));
  xor xor_1 (overfl, cout, full_adder_2_cout);
endmodule
