// Digital circuit micpro.dig as structural Verilog
module micpro (
  input  [3:0] data__in,
  input  clk,
  input  reset,
  output [3:0] alu__out,
  output [3:0] accum
);

  wire not_1_out;
  wire [1:0] step__reg;
  wire [3:0] accum__mux_y, data__mux_y, four_bit_mux_1_y, instr__reg, mar, pc, program_ram_1_data__out;
  wire [13:0] rom__out;

  not not_1 (not_1_out, rom__out[9]);
  program_ctr program_ctr_1 (.enable(rom__out[9]), .reset(reset), .clk(clk), .q(pc));
  four_bit_reg u_MAR (.d(accum__mux_y), .enable(rom__out[8]), .reset(reset), .clk(clk), .q(mar));
  four_bit_reg Instruction_Reg (.d(accum__mux_y), .enable(rom__out[0]), .reset(reset), .clk(clk), .q(instr__reg));
  two_bit_reg Step_Reg (.d(rom__out[13:12]), .enable(1'b1), .reset(reset), .clk(clk), .q(step__reg));
  four_bit_mux four_bit_mux_1 (.a(pc), .b(mar), .sel(not_1_out), .y(four_bit_mux_1_y));
  ROM #(.AddrBits(6), .Bits(14)) microcode_ROM (.A({instr__reg, step__reg}), .sel(1'b1), .D(rom__out));
  alu alu_1 (
    .a(accum__mux_y), .b(accum), .invert(rom__out[6]), .arith(rom__out[7]), .pass(rom__out[5]), .cin(1'b0),
    .y(alu__out));  // open: cout, overfl
  four_bit_reg accumulator (.d(alu__out), .enable(rom__out[4]), .reset(reset), .clk(clk), .q(accum));
  four_bit_mux accum__mux (.a(data__mux_y), .b(accum), .sel(rom__out[3]), .y(accum__mux_y));
  program_ram program_ram_1 (
    .addr(four_bit_mux_1_y), .data__in(accum__mux_y), .clk(clk), .write(rom__out[1]),
    .data__out(program_ram_1_data__out));
  four_bit_mux data__mux (.a(data__in), .b(program_ram_1_data__out), .sel(rom__out[2]), .y(data__mux_y));

  // Notes on the sheet:
  //   contents of microcode_ROM (hex, n*v repeats v):
  //   1205,234,0,0,1205,294,0,0,1205,1000,0,0,1205,214,0,0,1205,d8,0,0
  //   ,1205,2d4,0,0,1205,2304,a,0,1205,0,0,3fff
endmodule
