// Digital circuit test.dig as structural Verilog
module test (
  input  [3:0] in_1,
  input  [3:0] in_2,
  input  arith,
  input  invert,
  input  pass,
  input  loac__acc,
  input  acc__to__db,
  input  read,
  input  write,
  input  clk,
  input  reset,
  output [3:0] alu__out,
  output [3:0] accum,
  output [3:0] data__bus
);

  brainless brainless_1 (
    .addr__bus(in_1), .data__in(in_2), .arith(arith), .invert(invert), .pass(pass), .load__acc(loac__acc),
    .acc__to__db(acc__to__db), .read(read), .write(write), .clk(clk), .reset(reset), .alu__out(alu__out),
    .accum(accum), .data__bus(data__bus));
endmodule
